# Fritzing sketch MIDI Drums (saved by Fritzing 0.9.2b)
circuit board: 9.97186cm x 7.60118cm
breadboards: 1

parts:
  Nano = Arduino Nano (Rev3.0)
  switch1 = Rotary_Switch_12x1

nets:
  N1: Nano.GND, switch1.0
  N2: Nano.D2, switch1.1
  N3: Nano.D3, switch1.2
  N4: Nano.D4, switch1.3
  N5: Nano.D5, switch1.4
  N6: Nano.D6, switch1.5
